# Fritzing sketch BumperBot_Arduino_Nano (saved by Fritzing 0.9.6b)

parts:
  DC_Mot_Enc1 = DC Motor with two-phase hall-encoder [part_number=VT-E-G25A-06-177E]
  DC_Mot_Enc2 = DC Motor with two-phase hall-encoder [part_number=VT-E-G25A-06-177E]
  Raspberry_Pi_1 = Raspberry Pi 4 [part_number=RPI-4-b]  # not connected
  L298N2 = L298N DC motor driver
  M1 = RioRand LM2596
  U2 = LIPO-2000mAh [package=lipo-2000]
  Power_plug1 = USB-C plug
  USBTTL1 = Micro USB B Plug
  USBTTL2 = USB A Plug
  J1 = XT60 Connector male [package=THT]
  J2 = XT60 Connector female [package=THT]
  Part1 = Arduino Nano (Rev3.0)

nets:
  N1: DC_Mot_Enc1.pin1, L298N2.OUT3
  N2: DC_Mot_Enc1.pin3, Part1.D5
  N3: DC_Mot_Enc1.pin4, Part1.D3
  N4: DC_Mot_Enc1.pin5, DC_Mot_Enc2.pin5, Part1.3V3
  N5: DC_Mot_Enc1.pin6, L298N2.OUT4
  N6: DC_Mot_Enc2.pin1, L298N2.OUT2
  N7: DC_Mot_Enc2.pin3, Part1.D4
  N8: DC_Mot_Enc2.pin4, Part1.D2
  N9: DC_Mot_Enc2.pin6, L298N2.OUT1
  N10: L298N2.ENA, Part1.D9
  N11: L298N2.ENB, Part1.D11/MOSI
  N12: L298N2.IN1, Part1.D12/MISO
  N13: L298N2.IN2, Part1.D13/SCK
  N14: L298N2.IN3, Part1.D7
  N15: L298N2.IN4, Part1.D8
  N16: M1.Pin_1, J1.VCC
  N17: M1.Pin_2, J1.GND
  N18: M1.Pin_3, Power_plug1.VCC
  N19: M1.Pin_4, Power_plug1.GND
  N20: U2.+, J2.VCC
  N21: U2.-, J2.GND
  N22: USBTTL1.usb, USBTTL2.usb

custom parts:
  Raspberry Pi 4: The RPi4, a faster version of the awesome Raspberry Pi 2 B ARM Board with 40 pin gpio. Ready for special Raspberry Pi B+ and RPi2 Hat (Hardware attached (on) top)
  L298N DC motor driver: 2x DC motor driver with 78M05 positive voltage regulator (7..35 V) L298N: max 46 V, 2 A Set 5 V Enable jumper to enable 5 V regultor (needed for the L298N) and +5 V output at screw terminal or supply external +5 V at screw terminal Set ENA and/or ENB to +5 V to enable motor permanently or supply ENA and/or ENB with PWM signal IN1 and IN2 set rotation directory for motor A (OUT1/OUT2) IN2 and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
  USB-C plug: power plug
  XT60 Connector male: Yellow XT60 connector for high current loads up to 40A male
  XT60 Connector female: Yellow XT60 connector for high current loads up to 40A female
